// Logisim project BigASM_EJ3.circ as structural Verilog
module BOARD_BIG_ASM (
  output out_1
);

  wire button_1_out, CLK, CLR, d_ff_1_q, not_1_out, Write, Write_ASCII;
  wire [6:0] ASCII;
  wire [7:0] counter_1_q;
  wire [23:0] Dir_INPUT, Dir_MEMORY;
  wire [31:0] INPUT, MEMORY_IN, MEMORY_OUT;

  Button button_1 (.out(button_1_out));
  Clock clock_1 (.out(CLK));
  D_Flip_Flop d_ff_1 (.clk(CLK), .D(1'b1), .Q(d_ff_1_q), .reset(button_1_out));  // open: Qn, preset, en
  D_Flip_Flop d_ff_2 (.clk(CLK), .D(d_ff_1_q), .Qn(CLR), .reset(button_1_out));  // open: Q, preset, en
  BIG_ASM big_asm_1 (
    .DATA_INPUT(INPUT), .MEMORY_IN(MEMORY_OUT), .CLK(CLK), .CLR(CLR), .DIR_INPUT(Dir_INPUT),
    .MEMORY_OUT(MEMORY_IN), .DIR_MEMORY(Dir_MEMORY), .Write_OUTPUT(Write), .ASCII(ASCII),
    .Write_ASCII(Write_ASCII), .END(out_1));
  MEMORY memory_1 (.DIR(Dir_MEMORY), .DATA_IN(MEMORY_IN), .WRITE(Write), .CLK(CLK), .CLR(CLR), .DATA_OUT(MEMORY_OUT));
  INPUT input_1 (.DIR(Dir_INPUT), .CLK(CLK), .DATA_OUT(INPUT));
  Counter counter_1 (.load(1'b0), .count(not_1_out), .Q(counter_1_q), .clk(CLK), .clr(CLR));  // open: D, carry
  not not_1 (not_1_out, out_1);
  // Probe on counter_1_q
  TTY #(.rows(32), .cols(60)) tty_1 (.data(ASCII), .clk(CLK), .we(Write_ASCII), .clr(CLR));

  // Other names for the same wires on the sheet: END = out_1

  // Notes on the sheet:
  //   COUNTER
  //   BOARD
endmodule

module INPUT (
  input  [23:0] DIR,
  input  CLK,
  output [31:0] DATA_OUT
);

  RAM #(.addrWidth(24), .dataWidth(32)) ram_1 (.addr(DIR), .data(DATA_OUT), .clk(CLK), .ld(1'b1));  // open: sel, clr
endmodule

module MEMORY (
  input  [23:0] DIR,
  input  [31:0] DATA_IN,
  input  WRITE,
  input  CLK,
  input  CLR,
  output [31:0] DATA_OUT
);

  RAM #(.addrWidth(24), .dataWidth(32), .bus("separate")) ram_1 (
    .addr(DIR), .din(DATA_IN), .data(DATA_OUT), .str(WRITE), .clk(CLK), .clr(CLR));  // open: sel, ld
endmodule

module BIG_ASM (
  input  [31:0] DATA_INPUT,
  input  [31:0] MEMORY_IN,
  input  CLK,
  input  CLR,
  output [23:0] DIR_INPUT,
  output [31:0] MEMORY_OUT,
  output [23:0] DIR_MEMORY,
  output Write_OUTPUT,
  output [6:0] ASCII,
  output Write_ASCII,
  output END
);

  wire control_unit_1_e_count, control_unit_1_e_countdiv, control_unit_1_e_i, control_unit_1_e_j,
       control_unit_1_e_n, control_unit_1_s_count, control_unit_1_s_countdiv, control_unit_1_s_i,
       control_unit_1_s_j, datapath_1_count_____n, datapath_1_count___n, datapath_1_countdiv____1,
       datapath_1_i___j____0, datapath_1_j____i___2, Start;
  wire [31:0] datapath_1_i;

  DATAPATH datapath_1 (
    .Reloj(CLK), .Count_____n(datapath_1_count_____n), .Clean(CLR), .I___J____0(datapath_1_i___j____0),
    .E_Count(control_unit_1_e_count), .J____I___2(datapath_1_j____i___2), .E_I(control_unit_1_e_i),
    .Count___n(datapath_1_count___n), .E_J(control_unit_1_e_j), .CountDiv____1(datapath_1_countdiv____1),
    .S_CountDiv(control_unit_1_s_countdiv), .S_Count(control_unit_1_s_count), .S_I(control_unit_1_s_i),
    .S_J(control_unit_1_s_j), .N(DATA_INPUT), .E_CountDiv(control_unit_1_e_countdiv), .I(datapath_1_i),
    .E_N(control_unit_1_e_n));
  Starter starter_1 (.reloj(CLR), .clear(CLK), .Start(Start));
  CONTROL_UNIT control_unit_1 (
    .Count_____n(datapath_1_count_____n), .I___J____0(datapath_1_i___j____0),
    .S_CountDiv(control_unit_1_s_countdiv), .E_CountDiv(control_unit_1_e_countdiv),
    .J____I___2(datapath_1_j____i___2), .S_I(control_unit_1_s_i), .Count___n(datapath_1_count___n),
    .E_I(control_unit_1_e_i), .CountDiv____1(datapath_1_countdiv____1), .S_J(control_unit_1_s_j),
    .Reloj(CLK), .E_J(control_unit_1_e_j), .Clean(CLR), .S_Count(control_unit_1_s_count), .Start(Start),
    .E_Count(control_unit_1_e_count), .in_1(datapath_1_i), .WASCII(Write_ASCII), .END(END), .ASCII(ASCII),
    .E_N(control_unit_1_e_n));

  assign DIR_INPUT = {24{1'b0}};

  // Other names for the same wires on the sheet: Clean = CLR; reloj = CLK; WASCII = Write_ASCII

  // Notes on the sheet:
  //   L
  //   S
  //   S
  //   L
endmodule

module PRINT_UDEC (
  input  [31:0] num,
  input  start,
  input  CLK,
  input  RST,
  output [6:0] ASCII,
  output Write_ASCII,
  output \end 
);

  wire _0_c, _0_n, demultiplexer_1_out0, demultiplexer_2_out0, demultiplexer_2_out1, demultiplexer_3_out0,
       demultiplexer_3_out1, IDLE_2_q, IDLE_3_q, IDLE_4_q, IDLE_q, Lc, Lc_0, Ln, Ln_0, or_1_out;
  wire [23:0] bit_extender_1_out;
  wire [31:0] c, c___1, c___1_t, divider_1_rem, memory_1_data_out, multiplexer_1_out, multiplexer_2_out,
       multiplexer_3_out, n, n___10, n___10___48;

  Multiplexer #(.width(32), .enable("false")) multiplexer_1 (
    .in0(num), .in1(n___10), .out(multiplexer_1_out), .sel(Lc_0));
  Divider #(.width(32)) divider_1 (.a(n), .b(32'ha), .out(n___10), .rem(divider_1_rem));  // open: upper
  Adder #(.width(32)) adder_1 (.a(divider_1_rem), .b(32'h30), .out(n___10___48));  // open: cin, cout
  or or_1 (or_1_out, demultiplexer_1_out0, \end );
  Register #(.width(32)) u_n (.D(multiplexer_1_out), .en(Ln), .Q(n), .clk(CLK), .clr(RST));
  D_Flip_Flop IDLE (.clk(CLK), .D(or_1_out), .Q(IDLE_q), .preset(RST));  // open: Qn, en, reset
  Demultiplexer #(.enable("false")) demultiplexer_1 (
    .out0(demultiplexer_1_out0), .out1(Ln_0), .in(IDLE_q), .sel(start));
  or or_2 (Write_ASCII, demultiplexer_3_out0, demultiplexer_2_out1);
  Multiplexer #(.width(32), .enable("false")) multiplexer_2 (
    .in0(c___1), .in1(c___1_t), .out(multiplexer_2_out), .sel(Write_ASCII));
  Adder #(.width(32)) adder_2 (.a(c), .b(32'h1), .out(c___1));  // open: cin, cout
  Subtractor #(.width(32)) subtractor_1 (.a(c), .b(32'h1), .out(c___1_t));  // open: bin, bout
  D_Flip_Flop IDLE_2 (.clk(CLK), .D(Ln_0), .Q(IDLE_2_q), .reset(RST));  // open: Qn, preset, en
  Register #(.width(32)) u_c (.D(multiplexer_2_out), .en(Lc), .Q(c), .clk(CLK), .clr(RST));
  or or_3 (Lc_0, IDLE_2_q, demultiplexer_3_out1);
  Multiplexer #(.width(32), .enable("false")) multiplexer_3 (
    .in0(c), .in1(c___1_t), .out(multiplexer_3_out), .sel(Write_ASCII));
  Comparator #(.width(32), .mode("unsigned")) comparator_1 (.a({32{1'b0}}), .b(n), .lt(_0_n));  // open: gt, eq
  Comparator #(.width(32), .mode("unsigned")) comparator_2 (.a({32{1'b0}}), .b(c), .lt(_0_c));  // open: gt, eq
  D_Flip_Flop IDLE_3 (.clk(CLK), .D(Write_ASCII), .Q(IDLE_3_q), .reset(RST));  // open: Qn, preset, en
  Demultiplexer #(.enable("false")) demultiplexer_2 (
    .out0(demultiplexer_2_out0), .out1(demultiplexer_2_out1), .in(IDLE_3_q), .sel(_0_c));
  Bit_Extender #(.in_width(32), .out_width(24)) bit_extender_1 (.in(multiplexer_3_out), .out(bit_extender_1_out));
  D_Flip_Flop IDLE_4 (.clk(CLK), .D(Lc_0), .Q(IDLE_4_q), .reset(RST));  // open: Qn, preset, en
  or or_4 (Lc, Lc_0, Write_ASCII);
  or or_5 (Ln, Ln_0, Lc_0);
  Demultiplexer #(.enable("false")) demultiplexer_3 (
    .out0(demultiplexer_3_out0), .out1(demultiplexer_3_out1), .in(IDLE_4_q), .sel(_0_n));
  D_Flip_Flop IDLE_5 (.clk(CLK), .D(demultiplexer_2_out0), .Q(\end ), .reset(RST));  // open: Qn, preset, en
  MEMORY memory_1 (
    .DIR(bit_extender_1_out), .DATA_IN(n___10___48), .WRITE(Lc_0), .CLK(CLK), .CLR(RST),
    .DATA_OUT(memory_1_data_out));
  Bit_Extender #(.in_width(32), .out_width(7)) bit_extender_2 (.in(memory_1_data_out), .out(ASCII));

  // Other names for the same wires on the sheet: Lc_1 = Write_ASCII; Sc = Write_ASCII; Ln_1 = Lc_0; Sn = Lc_0;
  //   Write = Lc_0
endmodule

module PRINT_DEC (
  input  [31:0] num,
  input  start,
  input  CLK,
  input  RST,
  output [6:0] ASCII,
  output Write_ASCII,
  output END
);

  wire demultiplexer_1_out0, demultiplexer_1_out1, demultiplexer_2_out0, demultiplexer_3_out0, end_t,
       IDLE_3_q, IDLE_q, or_1_out, or_2_out, or_3_out, S_ASCII, startUDEC, Write_ASCII_1;
  wire [6:0] ASCII_t;
  wire [31:0] multiplexer_1_out, negator_1_out;

  or or_1 (or_1_out, demultiplexer_1_out0, END);
  Negator #(.width(32)) negator_1 (.in(num), .out(negator_1_out));
  D_Flip_Flop IDLE (.clk(CLK), .D(or_1_out), .Q(IDLE_q), .preset(RST));  // open: Qn, en, reset
  Demultiplexer #(.enable("false")) demultiplexer_1 (
    .out0(demultiplexer_1_out0), .out1(demultiplexer_1_out1), .in(IDLE_q), .sel(start));
  Multiplexer #(.width(32), .enable("false")) multiplexer_1 (
    .in0(num), .in1(negator_1_out), .out(multiplexer_1_out), .sel(num[31]));
  Demultiplexer #(.enable("false")) demultiplexer_2 (
    .out0(demultiplexer_2_out0), .out1(S_ASCII), .in(demultiplexer_1_out1), .sel(num[31]));
  or or_2 (or_2_out, demultiplexer_2_out0, S_ASCII);
  D_Flip_Flop IDLE_2 (.clk(CLK), .D(or_2_out), .Q(startUDEC), .reset(RST));  // open: Qn, preset, en
  PRINT_UDEC print_udec_1 (
    .num(multiplexer_1_out), .start(startUDEC), .CLK(CLK), .RST(RST), .ASCII(ASCII_t),
    .Write_ASCII(Write_ASCII_1), .\end (end_t));
  D_Flip_Flop IDLE_3 (.clk(CLK), .D(or_3_out), .Q(IDLE_3_q), .reset(RST));  // open: Qn, preset, en
  or or_3 (or_3_out, startUDEC, demultiplexer_3_out0);
  Demultiplexer #(.enable("false")) demultiplexer_3 (
    .out0(demultiplexer_3_out0), .out1(END), .in(IDLE_3_q), .sel(end_t));
  Multiplexer #(.width(7), .enable("false")) multiplexer_2 (
    .in0(ASCII_t), .in1(7'b0101101), .out(ASCII), .sel(S_ASCII));
  or or_4 (Write_ASCII, S_ASCII, Write_ASCII_1);

  // Other names for the same wires on the sheet: sign = num[31]; Write_ASCII_0 = S_ASCII
endmodule

module TEST_PRINT (
  input  [31:0] in_1,
  output out_2
);

  wire button_1_out, button_2_out, CLK, CLR, d_ff_1_q, Write_ASCII;
  wire [6:0] ASCII;

  Button button_1 (.out(button_1_out));
  Clock clock_1 (.out(CLK));
  D_Flip_Flop d_ff_1 (.clk(CLK), .D(1'b1), .Q(d_ff_1_q), .reset(button_1_out));  // open: Qn, preset, en
  D_Flip_Flop d_ff_2 (.clk(CLK), .D(d_ff_1_q), .Qn(CLR), .reset(button_1_out));  // open: Q, preset, en
  Button button_2 (.out(button_2_out));
  PRINT_UDEC print_udec_1 ();  // open: num, start, CLK, RST, ASCII, Write_ASCII, end
  PRINT_DEC print_dec_1 (
    .num(in_1), .start(button_2_out), .CLK(CLK), .RST(CLR), .ASCII(ASCII), .Write_ASCII(Write_ASCII),
    .END(out_2));
  TTY #(.rows(32), .cols(60)) tty_1 (.data(ASCII), .clk(CLK), .we(Write_ASCII), .clr(CLR));
endmodule

// DataPath
module DATAPATH (
  input  Clean,
  input  [31:0] N,
  input  Reloj,
  input  E_N,
  input  E_CountDiv,
  input  E_J,
  input  E_I,
  input  E_Count,
  input  S_CountDiv,
  input  S_Count,
  input  S_I,
  input  S_J,
  output [31:0] I,
  output Count_____n,
  output I___J____0,
  output J____I___2,
  output Count___n,
  output CountDiv____1
);

  wire comparator_3_eq, comparator_3_lt;
  wire [31:0] Count, Count___1, CountDiv, CountDiv___1, divider_1_rem, divider_2_out, I___1, J, J___1,
       multiplexer_1_out, multiplexer_2_out, multiplexer_3_out, multiplexer_4_out, N_t;

  Multiplexer #(.width(32), .enable("false")) multiplexer_1 (
    .in0({32{1'b0}}), .in1(CountDiv___1), .out(multiplexer_1_out), .sel(S_CountDiv));
  Register #(.width(32)) register_1 (.D(multiplexer_2_out), .en(E_Count), .Q(Count), .clk(Reloj), .clr(Clean));
  Multiplexer #(.width(32), .enable("false")) multiplexer_2 (
    .in0({32{1'b0}}), .in1(Count___1), .out(multiplexer_2_out), .sel(S_Count));
  Multiplexer #(.width(32), .enable("false")) multiplexer_3 (
    .in0(32'h2), .in1(I___1), .out(multiplexer_3_out), .sel(S_I));
  Register #(.width(32)) register_2 (.D(multiplexer_4_out), .en(E_J), .Q(J), .clk(Reloj), .clr(Clean));
  Multiplexer #(.width(32), .enable("false")) multiplexer_4 (
    .in0(32'h1), .in1(J___1), .out(multiplexer_4_out), .sel(S_J));
  Register #(.width(32)) register_3 (.D(N), .en(E_N), .Q(N_t), .clk(Reloj), .clr(Clean));
  Register #(.width(32)) register_4 (.D(multiplexer_3_out), .en(E_I), .Q(I), .clk(Reloj), .clr(Clean));
  Register #(.width(32)) register_5 (.D(multiplexer_1_out), .en(E_CountDiv), .Q(CountDiv), .clk(Reloj), .clr(Clean));
  Adder #(.width(32)) adder_1 (.a(Count), .b(32'h1), .out(Count___1));  // open: cin, cout
  Adder #(.width(32)) adder_2 (.a(I), .b(32'h1), .out(I___1));  // open: cin, cout
  Adder #(.width(32)) adder_3 (.a(J), .b(32'h1), .out(J___1));  // open: cin, cout
  Adder #(.width(32)) adder_4 (.a(CountDiv), .b(32'h1), .out(CountDiv___1));  // open: cin, cout
  Divider #(.width(32)) divider_1 (.a(I), .b(J), .rem(divider_1_rem));  // open: out, upper
  Comparator #(.width(32), .mode("unsigned")) comparator_1 (
    .a(Count), .b(N_t), .eq(Count_____n), .lt(Count___n));  // open: gt
  Divider #(.width(32)) divider_2 (.a(I), .b(32'h2), .out(divider_2_out));  // open: upper, rem
  Comparator #(.width(32), .mode("unsigned")) comparator_2 (
    .a(divider_1_rem), .b({32{1'b0}}), .eq(I___J____0));  // open: gt, lt
  Comparator #(.width(32), .mode("unsigned")) comparator_3 (
    .a(J), .b(divider_2_out), .eq(comparator_3_eq), .lt(comparator_3_lt));  // open: gt
  or or_1 (J____I___2, comparator_3_eq, comparator_3_lt);
  Comparator #(.width(32), .mode("unsigned")) comparator_4 (
    .a(CountDiv), .b(32'h1), .eq(CountDiv____1));  // open: gt, lt

  // Other names for the same wires on the sheet: Count____n = Count___n
endmodule

// Control Unit
module CONTROL_UNIT (
  input  [31:0] in_1,
  input  Start,
  input  Clean,
  input  Count_____n,
  input  I___J____0,
  input  J____I___2,
  input  Count___n,
  input  CountDiv____1,
  input  Reloj,
  output [6:0] ASCII,
  output WASCII,
  output END,
  output S_J,
  output S_I,
  output S_Count,
  output S_CountDiv,
  output E_Count,
  output E_I,
  output E_J,
  output E_CountDiv,
  output E_N
);

  wire d_ff_1_q, d_ff_2_q, d_ff_3_q, d_ff_4_q, d_ff_6_q, d_ff_7_q, d_ff_9_q, demultiplexer_1_out0,
       demultiplexer_2_out0, demultiplexer_3_out0, demultiplexer_3_out1, demultiplexer_4_out0,
       demultiplexer_4_out1, demultiplexer_5_out0, demultiplexer_6_out0, demultiplexer_7_out0,
       demultiplexer_7_out1, demultiplexer_8_out0, demultiplexer_8_out1, E_CountDiv0, or_1_out, or_2_out,
       or_3_out, or_4_out, or_7_out, or_10_out, or_11_out, or_12_out;

  or or_1 (or_1_out, demultiplexer_1_out0, demultiplexer_3_out1);
  D_Flip_Flop d_ff_1 (.clk(Reloj), .D(or_1_out), .Q(d_ff_1_q), .preset(Clean));  // open: Qn, en, reset
  Demultiplexer #(.enable("false")) demultiplexer_1 (
    .out0(demultiplexer_1_out0), .out1(E_N), .in(d_ff_1_q), .sel(Start));
  or or_2 (or_2_out, E_N, S_I);
  Demultiplexer #(.enable("false")) demultiplexer_2 (
    .out0(demultiplexer_2_out0), .out1(E_CountDiv0), .in(d_ff_2_q), .sel(Count___n));
  D_Flip_Flop d_ff_2 (.clk(Reloj), .D(or_2_out), .Q(d_ff_2_q), .reset(Clean));  // open: Qn, preset, en
  or or_3 (or_3_out, demultiplexer_3_out0, demultiplexer_2_out0);
  D_Flip_Flop d_ff_3 (.clk(Reloj), .D(or_3_out), .Q(d_ff_3_q), .reset(Clean));  // open: Qn, preset, en
  or or_4 (or_4_out, E_CountDiv0, S_J);
  Demultiplexer #(.enable("false")) demultiplexer_3 (
    .out0(demultiplexer_3_out0), .out1(demultiplexer_3_out1), .in(d_ff_3_q), .sel(Clean));
  Demultiplexer #(.enable("false")) demultiplexer_4 (
    .out0(demultiplexer_4_out0), .out1(demultiplexer_4_out1), .in(d_ff_4_q), .sel(J____I___2));
  D_Flip_Flop d_ff_4 (.clk(Reloj), .D(or_4_out), .Q(d_ff_4_q), .reset(Clean));  // open: Qn, preset, en
  or or_5 (E_I, E_N, S_I);
  Demultiplexer #(.enable("false")) demultiplexer_5 (
    .out0(demultiplexer_5_out0), .out1(S_CountDiv), .in(demultiplexer_4_out1), .sel(I___J____0));
  or or_6 (E_CountDiv, S_CountDiv, E_CountDiv0);
  or or_7 (or_7_out, demultiplexer_5_out0, S_CountDiv);
  or or_8 (E_J, E_CountDiv0, S_J);
  D_Flip_Flop d_ff_5 (.clk(Reloj), .D(or_7_out), .Q(S_J), .reset(Clean));  // open: Qn, preset, en
  or or_9 (E_Count, E_N, S_Count);
  Demultiplexer #(.enable("false")) demultiplexer_6 (
    .out0(demultiplexer_6_out0), .out1(S_Count), .in(demultiplexer_4_out0), .sel(CountDiv____1));
  D_Flip_Flop d_ff_6 (.clk(Reloj), .D(S_Count), .Q(d_ff_6_q), .reset(Clean));  // open: Qn, preset, en
  Demultiplexer #(.enable("false")) demultiplexer_7 (
    .out0(demultiplexer_7_out0), .out1(demultiplexer_7_out1), .in(d_ff_6_q), .sel(Count_____n));
  or or_10 (or_10_out, demultiplexer_7_out0, demultiplexer_8_out1);
  D_Flip_Flop d_ff_7 (.clk(Reloj), .D(or_10_out), .Q(d_ff_7_q), .reset(Clean));  // open: Qn, preset, en
  or or_11 (or_11_out, demultiplexer_6_out0, d_ff_7_q);
  or or_12 (or_12_out, demultiplexer_8_out0, demultiplexer_7_out1);
  D_Flip_Flop d_ff_8 (.clk(Reloj), .D(or_11_out), .Q(S_I), .reset(Clean));  // open: Qn, preset, en
  D_Flip_Flop d_ff_9 (.clk(Reloj), .D(or_12_out), .Q(d_ff_9_q), .reset(Clean));  // open: Qn, preset, en
  PRINT_UDEC print_udec_1 (
    .num(in_1), .start(demultiplexer_7_out1), .CLK(Reloj), .RST(Clean), .ASCII(ASCII), .Write_ASCII(WASCII),
    .\end (END));
  Demultiplexer #(.enable("false")) demultiplexer_8 (
    .out0(demultiplexer_8_out0), .out1(demultiplexer_8_out1), .in(d_ff_9_q), .sel(END));

  // Other names for the same wires on the sheet: E_Count1 = S_Count; E_CountDiv1 = S_CountDiv; E_Count0 = E_N;
  //   E_I0 = E_N; E_I1 = S_I; E_J0 = E_CountDiv0; E_J1 = S_J; I[31:0] = in_1

  // Notes on the sheet:
  //   Inicio
  //   Declarar Variables
  //   while count < n
  //   CountDiv = 0
  //   J = 0
  //   END
  //   while j <= i/2
  //   if I % J == 0
  //   CountDiv++
  //   J++
  //   if CountDiv == 1
  //   Count++
  //   if Count ==  n
  //   REPEAT CYCLE
  //   AFTER IF
  //   I++
  //   AFTER IF
endmodule

module Starter (
  input  reloj,
  input  clear,
  output Start
);

  wire d_ff_1_q, not_1_out;

  D_Flip_Flop d_ff_1 (.clk(reloj), .D(1'b1), .Q(d_ff_1_q), .en(not_1_out), .reset(clear));  // open: Qn, preset
  not not_1 (not_1_out, clear);
  nor nor_1 (Start, d_ff_1_q, clear);
endmodule
